# Fritzing sketch Untitled Sketch (saved by Fritzing 0.8.5b)
breadboards: 1

parts:
  M1 = Stepper Motor - Bipolar
  Componente1 = Arduino Uno (Rev3)
  U1 = mystery part, 16 pins [chip_label=? part_number=L293]
  R1 = Resistor [tolerance=±5% resistance=220 package=THT]
  LED1 = LED - 3mm [color="Red (633nm)" package="3 mm [THT]"]

nets:
  N1: M1.A, U1.pin6
  N2: M1.C, U1.pin3
  N3: M1.B, U1.pin11
  N4: M1.D, U1.pin14
  N5: Componente1.D9_PWM, U1.pin15
  N6: Componente1.D10_PWM/SS, U1.pin10
  N7: Componente1.D11_PWM/MOSI, U1.pin7
  N8: Componente1.D12/MISO, U1.pin2
  N9: Componente1.D2, LED1.anode
  N10: Componente1.5V, U1.pin1, U1.pin9, U1.pin16
  N11: Componente1.GND, U1.pin4, U1.pin5, U1.pin12, U1.pin13, R1.Pin_0
  N12: R1.Pin_1, LED1.cathode

notes:
  L293D
